// Digital circuit Template-02.dig as structural Verilog
module Template_02 (
  input  [2:0] In,
  input  clk,
  output [7:0] Z
);

  wire not_1_out, not_2_out, not_3_out;

  not not_1 (not_1_out, In[2]);
  not not_2 (not_2_out, In[0]);
  not not_3 (not_3_out, In[1]);
  Terminal terminal_1 (.D(Z), .C(clk), .en(1'b1));
endmodule
